# Fritzing sketch sintezator_scheme (saved by Fritzing 0.9.4)
breadboards: 1

parts:
  SD_разъём = MicroSD Card Module
  Микроконтроллер_Arduino_NANO = Arduino Nano (Rev3.0)
  Элемент_светодиодной_ленты_x360 = SMD RGB LED (WS2812) [package=5050]
  U2 = LIPO-2000mAh [package=lipo-2000]

nets:
  GND: SD_разъём.GND, Микроконтроллер_Arduino_NANO.GND, Элемент_светодиодной_ленты_x360.DOut, U2.-
  5V: SD_разъём.VCC, Микроконтроллер_Arduino_NANO.5V, Элемент_светодиодной_ленты_x360.VCC, U2.+
  N1: SD_разъём.MISO, Микроконтроллер_Arduino_NANO.D7
  N2: SD_разъём.MOSI, Микроконтроллер_Arduino_NANO.D8
  N3: SD_разъём.SCK, Микроконтроллер_Arduino_NANO.D9
  N4: SD_разъём.CS, Микроконтроллер_Arduino_NANO.D10
  N5: Микроконтроллер_Arduino_NANO.D6, Элемент_светодиодной_ленты_x360.DIn
  GND_2: Элемент_светодиодной_ленты_x360.VSS

notes:
  Блок питания
